# Fritzing sketch Master (saved by Fritzing 0.9.3b)
stripboards: 1

parts:
  WeMos_D1_Mini1 = WeMos D1 Mini  # not connected
  U1 = FS1000A - 433Mhz RF Transmitter [package=THT]
  U2 = XD-RF-5V [package=THT]
  J3 = female pin header, 4 pins [form="♀ (female)"]
  S2 = Pushbutton [package="[THT]"]
  J5 = male pin header, 2 pins [form="♂ (male)"]
  J6 = male pin header, 2 pins [form="♂ (male)"]  # not connected
  T1 = LM35 Temperature Sensor [package="TO92 [THT]"]
  R1 = Resistor [tolerance=±5% resistance=220 package=THT]
  S1 = Pushbutton [package="[THT]"]

nets:
  VCC: U1.VCC, U2.VCC, J3.pin2, J5.pin2, T1.+Vs, R1.Pin_1
  GND: U1.GND, U2.GND, J3.pin1, S2.Pin_3, S2.Pin_4, J5.pin1, T1.GND, S1.Pin_3, S1.Pin_4
  N1: S2.Pin_1, S2.Pin_2
  N2: T1.Vout, R1.Pin_0
  N3: S1.Pin_1, S1.Pin_2

custom parts:
  FS1000A - 433Mhz RF Transmitter: This is 433Mhz RF transmitter with receiver kit for Arduino ARM MCU wireless Application environment: Remote control switch, receiver module, motorcycles, automobile anti-theft products, home security products, electric doors, shutter doors, windows, remote control socket, remote control LED, remote audio remote control electric doors, garage door remote control, remote control retractable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
  XD-RF-5V: This is 433Mhz RF transmitter with receiver kit for Arduino ARM MCU wireless Application environment: Remote control switch, receiver module, motorcycles, automobile anti-theft products, home security products, electric doors, shutter doors, windows, remote control socket, remote control LED, remote audio remote control electric doors, garage door remote control, remote control retractable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
